// Logisim project 1805062.circ as structural Verilog: 1 circuit, main circuit main
module main (
  input  B,
  input  G,
  input  C,
  input  A,
  input  G_2,
  input  in_6,
  input  B_2,
  input  G_3,
  input  C_2,
  input  D,
  input  in_11,
  output out_12
);

  wire n74153_1_p7, n74153_2_p7, not_1_out;

  not not_1 (not_1_out, D);
  // _74153 74153_1: pin names not known; wires that end beside it: G, C, in_11, in_6, not_1_out, D, n74153_1_p7, B
  // _74153 74153_2: pin names not known; wires that end beside it: G_3, C_2, D, not_1_out, in_11, in_11, n74153_2_p7, B_2
  // _74157 74157_1: pin names not known; wires that end beside it: A, n74153_1_p7, n74153_2_p7, out_12, G_2
endmodule
