// Logisim project 1805062.circ as structural Verilog: 1 circuit, main circuit main
module main (
  input  D0,
  input  D1,
  input  D2,
  input  D3,
  output Y1,
  output Y0
);

  wire n7404_1_p3, n7404_1_p5, n7408_1_p6, n7408_1_p10;

  // _7404 7404_1: pin names not known; wires that end beside it: D2, D0, n7404_1_p3, D1, n7404_1_p5, 1'b0, 1'b1
  // _7408 7408_1: pin names not known; wires that end beside it: n7404_1_p3, n7404_1_p5, Y1, D3, n7404_1_p3, n7408_1_p6, 1'b1, n7404_1_p3, D1, n7408_1_p10
  // _7432 7432_1: pin names not known; wires that end beside it: 1'b0, n7408_1_p6, n7408_1_p10, Y0, 1'b0, 1'b1
endmodule
