// Logisim project Up-counter.circ as structural Verilog: 1 circuit, main circuit main
module main (
  input  y3,
  input  y2,
  input  y1,
  input  y0,
  output y3_2,
  output y2_2,
  output y1_2,
  output y0_2
);

  wire clock_1_out, n7408_1_p3, n7408_1_p4, n7408_1_p6, n7408_1_p7, n7408_1_p8, n7408_1_p9, n7408_2_p3,
       n7432_1_p3, n7432_1_p6, n7432_2_p3, n7432_2_p6, n7432_2_p7, n7432_2_p8;

  // _7408 7408_1: pin names not known; wires that end beside it: y3, y2, n7408_1_p3, n7408_1_p4, y0, n7408_1_p6, n7408_1_p7, n7408_1_p8, n7408_1_p9
  // _7404 7404_1: pin names not known; wires that end beside it: y1, n7408_1_p4, y2, n7408_1_p7, y0, n7408_1_p8
  // _7432 7432_1: pin names not known; wires that end beside it: n7408_1_p9, n7408_1_p6, n7432_1_p3, n7432_1_p3, n7408_1_p3, n7432_1_p6
  // _7432 7432_2: pin names not known; wires that end beside it: n7408_1_p8, n7408_1_p4, n7432_2_p3, n7432_2_p3, n7408_1_p7, n7432_2_p6, n7432_2_p7, n7432_2_p8
  Clock clock_1 (.out(clock_1_out));
  // _7408 7408_2: pin names not known; wires that end beside it: n7408_1_p7, n7432_2_p7, n7408_2_p3, y2, y1, y0, n7432_2_p7, y1
  // _7476 7476_1: pin names not known; wires that end beside it: clock_1_out, n7432_1_p6, clock_1_out, n7432_1_p6, y1_2, n7408_2_p3, y2_2, n7408_2_p3
  // _7476 7476_2: pin names not known; wires that end beside it: clock_1_out, n7432_2_p8, clock_1_out, n7432_2_p8, y3_2, n7432_2_p6, y0_2, n7432_2_p6

  // Notes on the sheet:
  //   T0
  //   T1
  //   T2
  //   T3
endmodule
