// Logisim project 1805062.circ as structural Verilog: 1 circuit, main circuit main
module main (
  input  T2,
  output Y2,
  output Y1,
  output Y0
);

  wire clock_1_out, n7408_1_p2, n7408_1_p3, n7432_1_p3, n7432_1_p5;

  Clock clock_1 (.out(clock_1_out));
  // _7408 7408_1: pin names not known; wires that end beside it: Y2, n7408_1_p2, n7408_1_p3, 1'b0, 1'b1
  // _7476 7476_1: pin names not known; wires that end beside it: clock_1_out, Y2, 1'b1, Y2, Y0, n7408_1_p2, 1'b0
  // _7432 7432_1: pin names not known; wires that end beside it: 1'b0, 1'b1, n7432_1_p3, n7408_1_p3, n7432_1_p5
  // _7476 7476_2: pin names not known; wires that end beside it: clock_1_out, T2, 1'b1, clock_1_out, T2, Y2, 1'b0, n7432_1_p5, Y1, n7432_1_p3, n7432_1_p5

  // Notes on the sheet:
  //   T0
  //   T1
endmodule
