// Logisim project 1805062.circ as structural Verilog: 1 circuit, main circuit main
module main (
  input  x1,
  input  x2,
  output z
);

  wire n7404_1_p5, n7408_1_p1, n7408_1_p2, n7408_1_p3, n7408_1_p4, n7408_1_p5, n7408_1_p6, n7408_1_p7,
       n7408_1_p9, n7408_2_p3, n7408_2_p6, n7408_2_p7, n7408_2_p9, n7408_2_p12, n7408_3_p1, n7408_3_p5,
       n7408_3_p10, n7432_1_p7, n7432_1_p10, n7474_1_p1;

  // _7408 7408_1: pin names not known; wires that end beside it: n7408_1_p1, n7408_1_p2, n7408_1_p3, n7408_1_p4, n7408_1_p5, n7408_1_p6, n7408_1_p7, n7408_1_p1, n7408_1_p9, n7408_1_p7, n7408_1_p5
  // _7404 7404_1: pin names not known; wires that end beside it: x1, n7408_1_p4, x2, n7408_1_p2, n7404_1_p5
  // _7408 7408_2: pin names not known; wires that end beside it: n7408_1_p4, n7408_1_p7, n7408_2_p3, x2, n7408_2_p3, n7408_2_p6, n7408_2_p7, n7408_1_p4, n7408_2_p9, x2, n7408_2_p7, n7408_2_p12
  // _7474 7474_1: pin names not known; wires that end beside it: n7474_1_p1, n7408_1_p7, n7408_1_p6, n7408_1_p9
  // _7408 7408_3: pin names not known; wires that end beside it: n7408_3_p1, n7408_1_p2, x1, n7408_3_p1, n7408_3_p5, x1, n7408_3_p1, n7408_3_p1, x2, n7408_3_p10
  // _7474 7474_2: pin names not known; wires that end beside it: n7408_2_p12, n7408_2_p7, n7408_3_p5
  // _7432 7432_1: pin names not known; wires that end beside it: n7408_2_p6, n7408_2_p6, n7408_2_p9, z, n7408_3_p10, n7404_1_p5, n7432_1_p7, n7408_3_p1, n7408_3_p1, n7432_1_p10
  // _7432 7432_2: pin names not known; wires that end beside it: n7408_1_p3, n7432_1_p10, n7474_1_p1, n7432_1_p7

  // Notes on the sheet:
  //   y0
  //   y2
endmodule
